// Logisim project ALSU.circ as structural Verilog: 1 circuit, main circuit main
module main (
);


  // Notes on the sheet:
  //   ALSU For Moris Mano Machine
  //   ALSU is just a combinational circuit that performs all the provided operations, and the one required is chosen.
endmodule
