// Logisim project Control_Unit.circ as structural Verilog: 1 circuit, main circuit Control_Unit
module Control_Unit (
  input  [15:0] IR,
  input  R,
  input  SC_INR,
  input  CP,
  input  CLR,
  output [11:0] Add
);

  wire and_1_out, and_2_out, decoder3x8_1_p1, decoder3x8_1_p2, decoder3x8_1_p3, decoder3x8_1_p4,
       decoder3x8_1_p5, decoder3x8_1_p7, decoder3x8_1_p9, decoder3x8_1_p11, decoder4x16_1_p1,
       decoder4x16_1_p2, decoder4x16_1_p3, decoder4x16_1_p4, decoder4x16_1_p5, decoder4x16_1_p6,
       decoder4x16_1_p7, decoder4x16_1_p8, decoder4x16_1_p9, decoder4x16_1_p10, decoder4x16_1_p11,
       decoder4x16_1_p12, decoder4x16_1_p13, decoder4x16_1_p14, decoder4x16_1_p15, decoder4x16_1_p16,
       decoder4x16_1_p17, decoder4x16_1_p18, decoder4x16_1_p19, decoder4x16_1_p20, not_1_out;

  // Decoder3x8 decoder3x8_1: pin names not known; wires that end beside it: decoder3x8_1_p1, decoder3x8_1_p2, decoder3x8_1_p3, decoder3x8_1_p4, decoder3x8_1_p5, IR[14], decoder3x8_1_p7, IR[13], decoder3x8_1_p9, IR[12], decoder3x8_1_p11
  // Decoder4x16 decoder4x16_1: pin names not known; wires that end beside it: decoder4x16_1_p1, decoder4x16_1_p2, decoder4x16_1_p3, decoder4x16_1_p4, decoder4x16_1_p5, decoder4x16_1_p6, decoder4x16_1_p7, decoder4x16_1_p8, decoder4x16_1_p9, decoder4x16_1_p10, decoder4x16_1_p11, decoder4x16_1_p12, decoder4x16_1_p13, decoder4x16_1_p14, decoder4x16_1_p15, decoder4x16_1_p16, decoder4x16_1_p17, decoder4x16_1_p18, decoder4x16_1_p19, decoder4x16_1_p20
  Bit4_Counter bit4_counter_1 (
    .INR(SC_INR), .CP(CP), .CLR(CLR), .A0(decoder4x16_1_p2), .A1(decoder4x16_1_p4), .A2(decoder4x16_1_p6),
    .A3(decoder4x16_1_p8));
  not not_1 (not_1_out, decoder3x8_1_p1);
  and and_1 (and_1_out, not_1_out, IR[15], decoder4x16_1_p5);
  and and_2 (and_2_out, decoder3x8_1_p1, decoder4x16_1_p5);
  AC_ControlUnit ac_controlunit_1 (
    .D0(decoder3x8_1_p11), .D1(decoder3x8_1_p9), .D2(decoder3x8_1_p7), .T5(decoder4x16_1_p9), .p(and_2_out),
    .r(and_1_out), .B9(IR[9]), .B7(IR[7]), .B6(IR[6]), .B5(IR[5]), .B11(IR[11]), .CLR(CLR));  // open: ACLD, ACINR, ACCLR
  AR_ControlUnit ar_controlunit_1 (
    .D7(decoder3x8_1_p1), .I(IR[15]), .T3(decoder4x16_1_p7), .T2(decoder4x16_1_p5), .R(R),
    .T0(decoder4x16_1_p1), .D5(decoder3x8_1_p3), .T4(decoder4x16_1_p9), .CLR(CLR));  // open: ARLD, ARINR, ARCLR
  DR_ControlUnit dr_controlunit_1 (
    .D0(decoder3x8_1_p11), .D1(decoder3x8_1_p9), .D2(decoder3x8_1_p7), .D6(decoder3x8_1_p2),
    .T4(decoder4x16_1_p9), .T5(decoder4x16_1_p10), .CLR(CLR));  // open: DRLD, DRINC, DRCLR
  IR_ControlUnit ir_controlunit_1 (.R(R), .T1(decoder4x16_1_p3), .CLR(CLR));  // open: IRLD, IRCLR
  Mem_ControlUnit mem_controlunit_1 (
    .D7(decoder3x8_1_p1), .I(IR[15]), .T3(decoder4x16_1_p7), .R(R), .T1(decoder4x16_1_p3),
    .D0(decoder3x8_1_p11), .D1(decoder3x8_1_p9), .D2(decoder3x8_1_p7), .D6(decoder3x8_1_p2),
    .T4(decoder4x16_1_p9), .T6(decoder4x16_1_p11), .D5(decoder3x8_1_p3), .D3(decoder3x8_1_p5));  // open: READ, WRITE
  PC_ControlUnit pc_controlunit_1 (
    .D4(decoder3x8_1_p4), .T4(decoder4x16_1_p7), .D5(decoder3x8_1_p3), .T5(decoder4x16_1_p9), .R(R),
    .T1(decoder4x16_1_p3), .T2(and_1_out), .B4(IR[11]), .AC_15(IR[9]), .B3(IR[5]), .AC_equals_0(CLR),
    .s_r(R), .p(decoder4x16_1_p1), .B9(CLR));  // open: B2, E_equals_0, B1, FGI, B8, FGO, D6, T6, DR_equals_0, CLR, PCLD, PCINR, PCCLR
  TR_ControlUnit tr_controlunit_1 (.R(R), .T0(decoder4x16_1_p1), .CLR(CLR));  // open: TRLD, TRINR, TRCLR

  assign Add = IR[11:0];

  // Notes on the sheet:
  //   Operation Decoder
  //   D
  //   Sequence Decoder
  //   T
  //   r = D7 I' T3
  //   p = D7 I T3
endmodule
