// Logisim project BasicComputer.circ as structural Verilog: 1 circuit, main circuit CompleteComputer
module CompleteComputer (
);

  wire and_1_out, bit16_alsu_1_p5, control_unit_1_acclr, control_unit_1_ace, control_unit_1_acinr,
       control_unit_1_acld, control_unit_1_alucin, control_unit_1_arclr, control_unit_1_are,
       control_unit_1_arinr, control_unit_1_arld, control_unit_1_cpe, control_unit_1_drclr,
       control_unit_1_dre, control_unit_1_drinc, control_unit_1_drld, control_unit_1_irclr,
       control_unit_1_ire, control_unit_1_irld, control_unit_1_meme, control_unit_1_pcclr,
       control_unit_1_pce, control_unit_1_pcinr, control_unit_1_pcld, control_unit_1_read,
       control_unit_1_scclr, control_unit_1_trclr, control_unit_1_tre, control_unit_1_trinr,
       control_unit_1_trld, control_unit_1_write, CP_out, Reset_out;
  wire [3:0] bit16_alsu_1_p1, bit16_alsu_1_p1_2, bit16_alsu_1_p1_3, bit16_alsu_1_p1_4, bit16_alsu_1_p2,
       bit16_alsu_1_p2_2, bit16_alsu_1_p2_3, bit16_alsu_1_p2_4, control_unit_1_alus, controlled_buffer_1_out,
       controlled_buffer_1_out_2, controlled_buffer_1_out_3, controlled_buffer_3_out, IR_a, IR_a_2, IR_a_3,
       IR_a_4, SC_a0;
  wire [7:0] INPR_a, OUTR_a;
  wire [11:0] AR_a, PC_a;
  wire [15:0] ram_1_dout, TR_a;

  Clock CP (.out(CP_out));
  and and_1 (and_1_out, control_unit_1_cpe, CP_out);
  Button Reset (.out(Reset_out));
  Bit4_Counter SC (
    .INR(1'b1), .CP(and_1_out), .CLR(control_unit_1_scclr), .A0(SC_a0[0]), .A1(SC_a0[1]), .A2(SC_a0[2]),
    .A3(SC_a0[3]));
  Hex_Digit_Display hex_digit_display_1 (.value(control_unit_1_alus));  // open: dp
  Control_Unit control_unit_1 (
    .IR({IR_a_4, IR_a_3, IR_a_2, IR_a}), .R(1'b0), .SC(SC_a0), .CLR(Reset_out), .ALUS(control_unit_1_alus),
    .ALUCin(control_unit_1_alucin), .SCCLR(control_unit_1_scclr), .ACLD(control_unit_1_acld),
    .ACINR(control_unit_1_acinr), .ACCLR(control_unit_1_acclr), .ARLD(control_unit_1_arld),
    .ARINR(control_unit_1_arinr), .ARCLR(control_unit_1_arclr), .DRLD(control_unit_1_drld),
    .DRINC(control_unit_1_drinc), .DRCLR(control_unit_1_drclr), .IRLD(control_unit_1_irld),
    .IRCLR(control_unit_1_irclr), .READ(control_unit_1_read), .WRITE(control_unit_1_write),
    .PCLD(control_unit_1_pcld), .PCINR(control_unit_1_pcinr), .PCCLR(control_unit_1_pcclr),
    .TRLD(control_unit_1_trld), .TRINR(control_unit_1_trinr), .TRCLR(control_unit_1_trclr),
    .ARE(control_unit_1_are), .PCE(control_unit_1_pce), .DRE(control_unit_1_dre), .ACE(control_unit_1_ace),
    .IRE(control_unit_1_ire), .TRE(control_unit_1_tre), .MEME(control_unit_1_meme), .CPE(control_unit_1_cpe));  // open: IEN, FGI, FGO, ELD, ECLR, ECMP, IENSET, IENCLR, SCLR, RSET, RCLR, FGICLR, FGOCLR
  Hex_Digit_Display hex_digit_display_2 (.value(SC_a0));  // open: dp
  // Bit16_ALSU bit16_alsu_1: pin names not known; wires that end beside it: {bit16_alsu_1_p1_4, bit16_alsu_1_p1_3, bit16_alsu_1_p1_2, bit16_alsu_1_p1}, {bit16_alsu_1_p2_4, bit16_alsu_1_p2_3, bit16_alsu_1_p2_2, bit16_alsu_1_p2}, control_unit_1_alus, control_unit_1_alucin, bit16_alsu_1_p5
  RAM #(.addrWidth(12), .asyncread("true"), .dataWidth(16)) ram_1 (
    .addr(AR_a), .we(control_unit_1_write), .oe(control_unit_1_read), .clk(and_1_out),
    .din({controlled_buffer_3_out, controlled_buffer_1_out_3, controlled_buffer_1_out_2, controlled_buffer_1_out}),
    .dout(ram_1_dout));
  // Master_Slave_Flip_Flop master_slave_flip_flop_1: pin names not known
  Bit12_Register AR (
    .I({controlled_buffer_1_out_3, controlled_buffer_1_out_2, controlled_buffer_1_out}),
    .Load(control_unit_1_arld), .INR(control_unit_1_arinr), .CLR(control_unit_1_arclr), .CP(and_1_out),
    .A(AR_a));  // open: C
  Bit12_Register PC (
    .I({controlled_buffer_1_out_3, controlled_buffer_1_out_2, controlled_buffer_1_out}),
    .Load(control_unit_1_pcld), .INR(control_unit_1_pcinr), .CLR(control_unit_1_pcclr), .CP(and_1_out),
    .A(PC_a));  // open: C
  Bit16_Register DR (
    .I({controlled_buffer_3_out, controlled_buffer_1_out_3, controlled_buffer_1_out_2, controlled_buffer_1_out}),
    .Load(control_unit_1_drld), .INR(control_unit_1_drinc), .CLR(control_unit_1_drclr), .CP(and_1_out),
    .A({bit16_alsu_1_p2_4, bit16_alsu_1_p2_3, bit16_alsu_1_p2_2, bit16_alsu_1_p2}));  // open: C
  // Bit16_Register AC: pin names not known; wires that end beside it: bit16_alsu_1_p5, control_unit_1_acld, control_unit_1_acinr, control_unit_1_acclr, and_1_out, {bit16_alsu_1_p1_4, bit16_alsu_1_p1_3, bit16_alsu_1_p1_2, bit16_alsu_1_p1}
  Bit8_Register INPR (.CLR(Reset_out), .CP(and_1_out), .A(INPR_a));  // open: I, Load, INR, C
  Bit16_Register IR (
    .I({controlled_buffer_3_out, controlled_buffer_1_out_3, controlled_buffer_1_out_2, controlled_buffer_1_out}),
    .Load(control_unit_1_irld), .INR(1'b0), .CLR(control_unit_1_irclr), .CP(and_1_out),
    .A({IR_a_4, IR_a_3, IR_a_2, IR_a}));  // open: C
  Bit16_Register TR (
    .I({controlled_buffer_3_out, controlled_buffer_1_out_3, controlled_buffer_1_out_2, controlled_buffer_1_out}),
    .Load(control_unit_1_trld), .INR(control_unit_1_trinr), .CLR(control_unit_1_trclr), .CP(and_1_out),
    .A(TR_a));  // open: C
  Bit8_Register OUTR (.CLR(Reset_out), .CP(and_1_out), .A(OUTR_a));  // open: I, Load, INR, C
  Hex_Digit_Display hex_digit_display_3 (.value(ram_1_dout[15:12]));  // open: dp
  Hex_Digit_Display hex_digit_display_4 (.value(ram_1_dout[11:8]));  // open: dp
  Hex_Digit_Display hex_digit_display_5 (.value(AR_a[11:8]));  // open: dp
  Hex_Digit_Display hex_digit_display_6 (.value(AR_a[7:4]));  // open: dp
  Hex_Digit_Display hex_digit_display_7 (.value(PC_a[11:8]));  // open: dp
  Hex_Digit_Display hex_digit_display_8 (.value(PC_a[7:4]));  // open: dp
  Hex_Digit_Display hex_digit_display_9 (.value(bit16_alsu_1_p2_4));  // open: dp
  Hex_Digit_Display hex_digit_display_10 (.value(bit16_alsu_1_p2_3));  // open: dp
  Hex_Digit_Display hex_digit_display_11 (.value(bit16_alsu_1_p1_4));  // open: dp
  Hex_Digit_Display hex_digit_display_12 (.value(bit16_alsu_1_p1_3));  // open: dp
  Hex_Digit_Display hex_digit_display_13 (.value(INPR_a[7:4]));  // open: dp
  Hex_Digit_Display hex_digit_display_14 (.value(INPR_a[3:0]));  // open: dp
  Hex_Digit_Display hex_digit_display_15 (.value(IR_a_4));  // open: dp
  Hex_Digit_Display hex_digit_display_16 (.value(IR_a_3));  // open: dp
  Hex_Digit_Display hex_digit_display_17 (.value(TR_a[15:12]));  // open: dp
  Hex_Digit_Display hex_digit_display_18 (.value(TR_a[11:8]));  // open: dp
  Hex_Digit_Display hex_digit_display_19 (.value(OUTR_a[7:4]));  // open: dp
  Hex_Digit_Display hex_digit_display_20 (.value(OUTR_a[3:0]));  // open: dp
  Hex_Digit_Display hex_digit_display_21 (.value(ram_1_dout[7:4]));  // open: dp
  Hex_Digit_Display hex_digit_display_22 (.value(ram_1_dout[3:0]));  // open: dp
  Hex_Digit_Display hex_digit_display_23 (.value(AR_a[3:0]));  // open: dp
  Hex_Digit_Display hex_digit_display_24 (.value(PC_a[3:0]));  // open: dp
  Hex_Digit_Display hex_digit_display_25 (.value(bit16_alsu_1_p2_2));  // open: dp
  Hex_Digit_Display hex_digit_display_26 (.value(bit16_alsu_1_p2));  // open: dp
  Hex_Digit_Display hex_digit_display_27 (.value(bit16_alsu_1_p1_2));  // open: dp
  Hex_Digit_Display hex_digit_display_28 (.value(bit16_alsu_1_p1));  // open: dp
  Hex_Digit_Display hex_digit_display_29 (.value(IR_a_2));  // open: dp
  Hex_Digit_Display hex_digit_display_30 (.value(IR_a));  // open: dp
  Hex_Digit_Display hex_digit_display_31 (.value(TR_a[7:4]));  // open: dp
  Hex_Digit_Display hex_digit_display_32 (.value(TR_a[3:0]));  // open: dp
  assign {controlled_buffer_1_out_3, controlled_buffer_1_out_2, controlled_buffer_1_out} = control_unit_1_are ? AR_a : 12'bz;  // Controlled_Buffer controlled_buffer_1
  assign {controlled_buffer_1_out_3, controlled_buffer_1_out_2, controlled_buffer_1_out} = control_unit_1_pce ? PC_a : 12'bz;  // Controlled_Buffer controlled_buffer_2
  assign {controlled_buffer_3_out, controlled_buffer_1_out_3, controlled_buffer_1_out_2, controlled_buffer_1_out} = control_unit_1_dre ? {bit16_alsu_1_p2_4, bit16_alsu_1_p2_3, bit16_alsu_1_p2_2, bit16_alsu_1_p2} : 16'bz;  // Controlled_Buffer controlled_buffer_3
  Hex_Digit_Display hex_digit_display_33 (.value(controlled_buffer_3_out));  // open: dp
  assign {controlled_buffer_3_out, controlled_buffer_1_out_3, controlled_buffer_1_out_2, controlled_buffer_1_out} = control_unit_1_ace ? {bit16_alsu_1_p1_4, bit16_alsu_1_p1_3, bit16_alsu_1_p1_2, bit16_alsu_1_p1} : 16'bz;  // Controlled_Buffer controlled_buffer_4
  Hex_Digit_Display hex_digit_display_34 (.value(controlled_buffer_1_out_3));  // open: dp
  Hex_Digit_Display hex_digit_display_35 (.value(controlled_buffer_1_out_2));  // open: dp
  assign {controlled_buffer_3_out, controlled_buffer_1_out_3, controlled_buffer_1_out_2, controlled_buffer_1_out} = control_unit_1_ire ? {IR_a_4, IR_a_3, IR_a_2, IR_a} : 16'bz;  // Controlled_Buffer controlled_buffer_5
  assign {controlled_buffer_3_out, controlled_buffer_1_out_3, controlled_buffer_1_out_2, controlled_buffer_1_out} = control_unit_1_meme ? ram_1_dout : 16'bz;  // Controlled_Buffer controlled_buffer_6
  Hex_Digit_Display hex_digit_display_36 (.value(controlled_buffer_1_out));  // open: dp
  assign {controlled_buffer_3_out, controlled_buffer_1_out_3, controlled_buffer_1_out_2, controlled_buffer_1_out} = control_unit_1_tre ? TR_a : 16'bz;  // Controlled_Buffer controlled_buffer_7
endmodule
